# Fritzing sketch my model train (saved by Fritzing 0.9.3b)
circuit board: 8.46667cm x 5.64444cm
breadboards: 1

parts:
  Part1 = motor driver L9110
  Part2 = Bluetooth HC-05 Macho
  Part3 = Arduino Nano (Rev3.0)
  BATT1 = 4xAA Switchable Battery Pack w/JST connector
  M1 = DC Motor

nets:
  GND: Part1.GND, Part2.GND, Part3.GND, BATT1.NEG
  VCC: Part1.VCC, Part3.VIN, BATT1.POS
  N1: Part1.A-i-1, Part3.D10
  N2: Part1.A-i-2, Part3.D9
  N3: Part1.A-o-1, M1.pin_1
  N4: Part1.A-o-2, M1.pin_2
  N5: Part2.TXD, Part3.D8
  N6: Part2.RXD, Part3.D7
  VCC_2: Part2.VCC, Part3.5V

custom parts:
  motor driver L9110: dc motor driver L9110
  4xAA Switchable Battery Pack w/JST connector: 4xAA Switchable Battery Pack with JST connector
